// Logisim project basic computer.circ as structural Verilog: 8 circuits, main circuit register_16bit
module BUS (
  input  [7:0] INPR,
  output [11:0] out_2,
  output [11:0] out_3,
  output [15:0] out_4,
  output [15:0] out_5,
  output [15:0] out_6,
  output [7:0] out_7,
  output [15:0] out_8,
  output [15:0] out_9,
  output [15:0] out_10,
  output [7:0] out_11,
  output [7:0] out_12,
  output [2:0] out_13
);

  wire AC_0, AC_CLR, AC_INR, AC_LD, and_2_out, and_3_out, and_4_out, and_6_out, and_7_out, and_8_out,
       and_9_out, and_10_out, and_11_out, and_12_out, and_13_out, and_14_out, and_15_out, and_16_out,
       and_17_out, and_18_out, and_19_out, and_20_out, and_21_out, and_22_out, and_23_out, and_24_out,
       and_27_out, and_28_out, and_29_out, and_30_out, and_31_out, and_32_out, and_37_out, and_38_out,
       and_41_out, and_42_out, and_43_out, and_44_out, and_45_out, and_48_out, and_49_out, and_50_out,
       and_51_out, and_52_out, and_53_out, and_54_out, and_55_out, and_56_out, and_57_out, and_63_out,
       and_64_out, and_66_out, and_67_out, and_68_out, and_71_out, and_72_out, and_73_out, and_74_out,
       and_75_out, and_76_out, and_77_out, and_78_out, and_79_out, AR_CLR, AR_INR, AR_LD, CLK, clock_1_out,
       D0, D1, D2, D3, D4, D5, D6, D7, DR_0, DR_INR, DR_LD, E, E_OUT, E_RESET, E_SET, FGI, FGI_FGO_RESET,
       FGI_NOT, FGI_SET, FGO, FGO_SET, FOG_or_FGI, I_Q, I_Q__NOT, IEN, IEN_RESET, IEN_SET, IR_LD, nor_1_out,
       not_1_out, not_2_out, not_3_out, not_4_out, not_5_out, not_6_out, not_7_out, not_8_out, not_9_out,
       or_1_out, OUTR_LD, P, PC_CLR, PC_INR, PC_LD, r, R_Q, R_Q__NOT, R_RESET, R_SET, read, S_Q, S_SET,
       SC_LD, T0, T1, T2, T3, T4, T5, T6, T7, T8, T9, T10, T11, T12, T13, T14, T15, TR_LD, write, X1, X2, X3,
       X4, X5, X6, X7;
  wire [3:0] SC_q;
  wire [6:0] AC_CNTRL;
  wire [15:0] ALU_out;

  Clock clock_1 (.out(clock_1_out));
  and and_1 (CLK, clock_1_out, ~S_Q);  // AND_Gate
  not not_1 (not_1_out, SC_LD);
  Counter #(.width(4), .max('hf)) SC (
    .load(SC_LD), .D(4'b0000), .count(not_1_out), .Q(SC_q), .clk(CLK));  // open: carry, clr
  and and_2 (and_2_out, T3, D7, I_Q__NOT);
  Decoder #(.select(4), .enable("false")) decoder_1 (
    .out0(T0), .out1(T1), .out2(T2), .out3(T3), .out4(T4), .out5(T5), .out6(T6), .out7(T7), .out8(T8),
    .out9(T9), .out10(T10), .out11(T11), .out12(T12), .out13(T13), .out14(T14), .out15(T15), .sel(SC_q));
  and and_3 (and_3_out, out_8[8], and_2_out);
  and and_4 (and_4_out, and_2_out, out_8[10]);
  or or_1 (or_1_out, and_3_out, and_4_out);
  and and_5 (S_SET, r, out_8[0]);
  and and_6 (and_6_out, D0, T5);
  and and_7 (and_7_out, R_Q, T2);
  and and_8 (and_8_out, D1, T5);
  and and_9 (and_9_out, D2, T5);
  and and_10 (and_10_out, D3, T4);
  and and_11 (and_11_out, D4, T4);
  and and_12 (and_12_out, D5, T5);
  and and_13 (and_13_out, D6, T6);
  not not_2 (not_2_out, or_1_out);
  nor nor_1 (nor_1_out, T2, T1, T0);
  not not_3 (not_3_out, E_OUT);
  and and_14 (and_14_out, E_OUT, not_2_out);
  and and_15 (and_15_out, not_2_out, not_3_out);
  ALU ALU (.DR(out_4), .AC(out_5), .INPR(out_7), .E(E), .OUT(ALU_out), .CNTRL(AC_CNTRL), .E_OUT(E_OUT));
  and and_16 (and_16_out, D4, T4);
  and and_17 (and_17_out, T5, D5);
  and and_18 (and_18_out, R_Q__NOT, T0);
  and and_19 (and_19_out, R_Q, T0);
  and and_20 (and_20_out, T4, D5);
  and and_21 (and_21_out, T5, D2);
  and and_22 (and_22_out, T6, D6);
  and and_23 (and_23_out, T4, D3);
  and and_24 (and_24_out, P, out_8[10]);
  and and_25 (X5, T2, R_Q__NOT);
  and and_26 (X6, R_Q, T1);
  and and_27 (and_27_out, R_Q__NOT, T1);
  and and_28 (and_28_out, ~D7, I_Q, T3);  // AND_Gate
  and and_29 (and_29_out, D0, T4);
  and and_30 (and_30_out, D1, T4);
  and and_31 (and_31_out, D2, T4);
  and and_32 (and_32_out, D6, T4);
  Decoder #(.select(3), .enable("false")) decoder_2 (
    .out0(D0), .out1(D1), .out2(D2), .out3(D3), .out4(D4), .out5(D5), .out6(D6), .out7(D7), .sel(out_8[14:12]));
  and and_33 (FGI_FGO_RESET, P, out_8[11]);
  or or_2 (E_SET, and_14_out, and_3_out);
  or or_3 (E_RESET, and_3_out, and_4_out, and_15_out);
  or or_4 (X1, and_16_out, and_17_out);
  or or_5 (X2, and_18_out, and_19_out, and_20_out);
  or or_6 (X3, and_21_out, and_22_out);
  or or_7 (X4, and_23_out, and_24_out);
  or or_8 (SC_LD, and_6_out, and_7_out, and_8_out, and_9_out, and_10_out, and_11_out, and_12_out, and_13_out, r, P);
  and and_34 (R_SET, nor_1_out, IEN, FOG_or_FGI);
  and and_35 (R_RESET, R_Q, T2);
  or or_9 (X7, and_27_out, and_28_out, and_29_out, r, and_30_out, and_31_out, and_32_out);
  INPR u_INPR (.INPUT(INPR), .OUTPUT(out_7), .FGI_NOT(FGI_NOT));
  RAM #(.addrWidth(12), .dataWidth(16), .bus("separate")) ram_1 (
    .addr(out_2), .din(out_6), .data(out_10), .str(write), .clk(CLK), .ld(read));  // open: sel, clr
  OUTR OUTR (.in_2(out_6[7:0]), .LD(OUTR_LD), .out_4(out_11), .CLK(CLK));
  and and_36 (IEN_SET, P, out_8[7]);
  and and_37 (and_37_out, P, out_8[6]);
  and and_38 (and_38_out, R_Q, T2);
  register_12bit AR (.LD(AR_LD), .in_2(out_6[11:0]), .out_6(out_2), .INR(AR_INR), .CLR(AR_CLR), .CLK(CLK));
  register_12bit PC (.LD(PC_LD), .in_2(out_6[11:0]), .out_6(out_3), .INR(PC_INR), .CLR(PC_CLR), .CLK(CLK));
  register_16bit DR (.LD(DR_LD), .in_2(out_6), .out_6(out_4), .INR(DR_INR), .CLR(1'b0), .CLK(CLK));
  register_16bit AC (.LD(AC_LD), .in_2(ALU_out), .out_6(out_5), .INR(AC_INR), .CLR(AC_CLR), .CLK(CLK));
  register_16bit IR (.LD(IR_LD), .in_2(out_6), .out_6(out_8), .INR(1'b0), .CLR(1'b0), .CLK(CLK));
  register_16bit TR (.LD(TR_LD), .in_2(out_6), .out_6(out_9), .INR(1'b0), .CLR(1'b0), .CLK(CLK));
  or or_10 (IEN_RESET, and_37_out, and_38_out);
  or or_11 (FGI_SET, out_7[0], out_7[1], out_7[2], out_7[3], out_7[4], out_7[5], out_7[6], out_7[7]);
  or or_12 (FGO_SET, out_11[0], out_11[1], out_11[2], out_11[3], out_11[4], out_11[5], out_11[6], out_11[7]);
  and and_39 (r, D7, I_Q__NOT, T3);
  and and_40 (P, D7, I_Q, T3);
  or or_13 (DR_0, out_4[0], out_4[1], out_4[2], out_4[3], out_4[4], out_4[5], out_4[6], out_4[7], out_4[8], out_4[9], out_4[10], out_4[11], out_4[12], out_4[13], out_4[14], out_4[15]);
  or or_14 (AC_0, out_5[0], out_5[1], out_5[2], out_5[3], out_5[4], out_5[5], out_5[6], out_5[7], out_5[8], out_5[9], out_5[10], out_5[11], out_5[12], out_5[13], out_5[14], out_5[15]);
  J_K_Flip_Flop u_IEN (.J(IEN_SET), .clk(CLK), .K(IEN_RESET), .Q(IEN));  // open: Qn, preset, en, reset
  J_K_Flip_Flop u_FGI (.J(FGI_SET), .clk(CLK), .K(FGI_FGO_RESET), .Q(FGI), .Qn(FGI_NOT));  // open: preset, en, reset
  J_K_Flip_Flop u_FGO (.J(FGO_SET), .clk(CLK), .K(FGI_FGO_RESET), .Q(FGO));  // open: Qn, preset, en, reset
  or or_15 (FOG_or_FGI, FGI, FGO);
  not not_4 (not_4_out, R_Q);
  Multiplexer #(.select(3), .enable("false")) multiplexer_1 (
    .in0(1'b0), .in1(out_2[0]), .in2(out_3[0]), .in3(out_4[0]), .in4(out_5[0]), .in5(out_8[0]),
    .in6(out_9[0]), .in7(out_10[0]), .out(out_6[0]), .sel(out_13));
  Multiplexer #(.select(3), .enable("false")) multiplexer_2 (
    .in0(1'b0), .in1(out_2[1]), .in2(out_3[1]), .in3(out_4[1]), .in4(out_5[1]), .in5(out_8[1]),
    .in6(out_9[1]), .in7(out_10[1]), .out(out_6[1]), .sel(out_13));
  Multiplexer #(.select(3), .enable("false")) multiplexer_3 (
    .in0(1'b0), .in1(out_2[2]), .in2(out_3[2]), .in3(out_4[2]), .in4(out_5[2]), .in5(out_8[2]),
    .in6(out_9[2]), .in7(out_10[2]), .out(out_6[2]), .sel(out_13));
  Multiplexer #(.select(3), .enable("false")) multiplexer_4 (
    .in0(1'b0), .in1(out_2[3]), .in2(out_3[3]), .in3(out_4[3]), .in4(out_5[3]), .in5(out_8[3]),
    .in6(out_9[3]), .in7(out_10[3]), .out(out_6[3]), .sel(out_13));
  Multiplexer #(.select(3), .enable("false")) multiplexer_5 (
    .in0(1'b0), .in1(out_2[4]), .in2(out_3[4]), .in3(out_4[4]), .in4(out_5[4]), .in5(out_8[4]),
    .in6(out_9[4]), .in7(out_10[4]), .out(out_6[4]), .sel(out_13));
  Multiplexer #(.select(3), .enable("false")) multiplexer_6 (
    .in0(1'b0), .in1(out_2[5]), .in2(out_3[5]), .in3(out_4[5]), .in4(out_5[5]), .in5(out_8[5]),
    .in6(out_9[5]), .in7(out_10[5]), .out(out_6[5]), .sel(out_13));
  Multiplexer #(.select(3), .enable("false")) multiplexer_7 (
    .in0(1'b0), .in1(out_2[6]), .in2(out_3[6]), .in3(out_4[6]), .in4(out_5[6]), .in5(out_8[6]),
    .in6(out_9[6]), .in7(out_10[6]), .out(out_6[6]), .sel(out_13));
  Multiplexer #(.select(3), .enable("false")) multiplexer_8 (
    .in0(1'b0), .in1(out_2[7]), .in2(out_3[7]), .in3(out_4[7]), .in4(out_5[7]), .in5(out_8[7]),
    .in6(out_9[7]), .in7(out_10[7]), .out(out_6[7]), .sel(out_13));
  Multiplexer #(.select(3), .enable("false")) multiplexer_9 (
    .in0(1'b0), .in1(out_2[8]), .in2(out_3[8]), .in3(out_4[8]), .in4(out_5[8]), .in5(out_8[8]),
    .in6(out_9[8]), .in7(out_10[8]), .out(out_6[8]), .sel(out_13));
  Multiplexer #(.select(3), .enable("false")) multiplexer_10 (
    .in0(1'b0), .in1(out_2[9]), .in2(out_3[9]), .in3(out_4[9]), .in4(out_5[9]), .in5(out_8[9]),
    .in6(out_9[9]), .in7(out_10[9]), .out(out_6[9]), .sel(out_13));
  Multiplexer #(.select(3), .enable("false")) multiplexer_11 (
    .in0(1'b0), .in1(out_2[10]), .in2(out_3[10]), .in3(out_4[10]), .in4(out_5[10]), .in5(out_8[10]),
    .in6(out_9[10]), .in7(out_10[10]), .out(out_6[10]), .sel(out_13));
  Multiplexer #(.select(3), .enable("false")) multiplexer_12 (
    .in0(1'b0), .in1(out_2[11]), .in2(out_3[11]), .in3(out_4[11]), .in4(out_5[11]), .in5(out_8[11]),
    .in6(out_9[11]), .in7(out_10[11]), .out(out_6[11]), .sel(out_13));
  Multiplexer #(.select(3), .enable("false")) multiplexer_13 (
    .in0(1'b0), .in1(1'b0), .in2(1'b0), .in3(out_4[12]), .in4(out_5[12]), .in5(out_8[12]), .in6(out_9[12]),
    .in7(out_10[12]), .out(out_6[12]), .sel(out_13));
  Multiplexer #(.select(3), .enable("false")) multiplexer_14 (
    .in0(1'b0), .in1(1'b0), .in2(1'b0), .in3(out_4[13]), .in4(out_5[13]), .in5(out_8[13]), .in6(out_9[13]),
    .in7(out_10[13]), .out(out_6[13]), .sel(out_13));
  Multiplexer #(.select(3), .enable("false")) multiplexer_15 (
    .in0(1'b0), .in1(1'b0), .in2(1'b0), .in3(out_4[14]), .in4(out_5[14]), .in5(out_8[14]), .in6(out_9[14]),
    .in7(out_10[14]), .out(out_6[14]), .sel(out_13));
  Multiplexer #(.select(3), .enable("false")) multiplexer_16 (
    .in0(1'b0), .in1(1'b0), .in2(1'b0), .in3(out_4[15]), .in4(out_5[15]), .in5(out_8[15]), .in6(out_9[15]),
    .in7(out_10[15]), .out(out_6[15]), .sel(out_13));
  Priority_Encoder priority_encoder_1 (
    .in0(1'b0), .in1(X1), .in2(X2), .in3(X3), .in4(X4), .in5(X5), .in6(X6), .in7(X7), .out(out_13));  // open: en_in, gs, en_out
  not not_5 (not_5_out, D7);
  and and_41 (and_41_out, R_Q__NOT, T3);
  D_Flip_Flop I (.clk(CLK), .D(out_8[15]), .Q(I_Q), .Qn(I_Q__NOT), .en(and_41_out));  // open: preset, reset
  J_K_Flip_Flop u_R (.J(R_SET), .clk(CLK), .K(R_RESET), .Q(R_Q), .Qn(R_Q__NOT));  // open: preset, en, reset
  and and_42 (and_42_out, D0, T4);
  and and_43 (and_43_out, D1, T4);
  and and_44 (and_44_out, D2, T4);
  and and_45 (and_45_out, D6, T4);
  and and_46 (DR_INR, T5, D6);
  and and_47 (TR_LD, R_Q, T0);
  and and_48 (and_48_out, not_4_out, T1);
  and and_49 (and_49_out, not_5_out, I_Q, T3);
  and and_50 (and_50_out, D0, T4);
  and and_51 (and_51_out, D1, T4);
  and and_52 (and_52_out, D2, T4);
  and and_53 (and_53_out, D6, T4);
  and and_54 (and_54_out, R_Q, T1);
  and and_55 (and_55_out, D3, T4);
  and and_56 (and_56_out, D5, T4);
  and and_57 (and_57_out, D6, T6);
  or or_16 (DR_LD, and_42_out, and_43_out, and_44_out, and_45_out);
  and AND_58 (AC_CNTRL[0], D0, T5);
  and ADD (AC_CNTRL[1], D1, T5);
  and DR_2 (AC_CNTRL[2], D2, T5);
  and INPR_2 (AC_CNTRL[3], P, out_8[11]);
  and COM (AC_CNTRL[4], r, out_8[9]);
  and SHR (AC_CNTRL[5], r, out_8[7]);
  and SHL (AC_CNTRL[6], r, out_8[6]);
  and and_59 (AC_CLR, r, out_8[11]);
  and and_60 (AC_INR, r, out_8[5]);
  and and_61 (IR_LD, R_Q__NOT, T1);
  and and_62 (OUTR_LD, P, out_8[10]);
  and and_63 (and_63_out, D4, T4);
  and and_64 (and_64_out, D5, T5);
  and and_65 (PC_CLR, R_Q, T1);
  not not_6 (not_6_out, DR_0);
  not not_7 (not_7_out, out_5[15]);
  and and_66 (and_66_out, T0, R_Q__NOT);
  and and_67 (and_67_out, R_Q__NOT, T2);
  and and_68 (and_68_out, ~D7, I_Q, T3);  // AND_Gate
  and and_69 (AR_CLR, R_Q, T0);
  and and_70 (AR_INR, D5, T4);
  and and_71 (and_71_out, R_Q, T2);
  and and_72 (and_72_out, D6, T6, not_6_out);
  and and_73 (and_73_out, not_7_out, r, out_8[4]);
  and and_74 (and_74_out, out_5[15], r, out_8[3]);
  not not_8 (not_8_out, AC_0);
  and and_75 (and_75_out, not_8_out, r, out_8[2]);
  not not_9 (not_9_out, E);
  and and_76 (and_76_out, not_9_out, r, out_8[1]);
  and and_77 (and_77_out, FGO, P, out_8[8]);
  and and_78 (and_78_out, FGI, P, out_8[9]);
  and and_79 (and_79_out, T1, R_Q__NOT);
  or or_17 (read, and_48_out, and_49_out, and_50_out, and_51_out, and_52_out, and_53_out);
  or or_18 (write, and_54_out, and_55_out, and_56_out, and_57_out);
  or or_19 (AR_LD, and_66_out, and_67_out, and_68_out);
  or or_20 (PC_LD, and_63_out, and_64_out);
  or or_21 (PC_INR, and_71_out, and_72_out, and_73_out, and_74_out, and_75_out, and_76_out, and_77_out, and_78_out, and_79_out);
  or or_22 (AC_LD, AC_CNTRL[0], AC_CNTRL[1], AC_CNTRL[2], AC_CNTRL[3], AC_CNTRL[4], AC_CNTRL[5], AC_CNTRL[6]);
  J_K_Flip_Flop u_E (.J(E_SET), .clk(CLK), .K(E_RESET), .Q(E));  // open: Qn, preset, en, reset
  J_K_Flip_Flop S (.J(S_SET), .clk(CLK), .K(1'b0), .Q(S_Q));  // open: Qn, preset, en, reset

  assign out_12 = out_6[7:0];

  // Other names for the same wires on the sheet: IR[15:0] = out_8; IR_12 = out_8[12]; IR_13 = out_8[13];
  //   IR_14 = out_8[14]; B0 = out_8[0]; IR_0 = out_8[0]; B1 = out_8[1]; IR_1 = out_8[1]; B2 = out_8[2];
  //   IR_2 = out_8[2]; B3 = out_8[3]; IR_3 = out_8[3]; B4 = out_8[4]; IR_4 = out_8[4]; B5 = out_8[5]; IR_5 = out_8[5];
  //   B6 = out_8[6]; IR_6 = out_8[6]; B7 = out_8[7]; IR_7 = out_8[7]; B8 = out_8[8]; IR_8 = out_8[8]; B9 = out_8[9];
  //   IR_9 = out_8[9]; B10 = out_8[10]; IR_10 = out_8[10]; B11 = out_8[11]; IR_11 = out_8[11]; I = out_8[15];
  //   IR_15 = out_8[15]; AR_0 = out_2[0]; AR_1 = out_2[1]; AR_2 = out_2[2]; AR_3 = out_2[3]; AR_4 = out_2[4];
  //   AR_5 = out_2[5]; AR_6 = out_2[6]; AR_7 = out_2[7]; AR_8 = out_2[8]; AR_9 = out_2[9]; AR_10 = out_2[10];
  //   AR_11 = out_2[11]; PC_0 = out_3[0]; PC_1 = out_3[1]; PC_2 = out_3[2]; PC_3 = out_3[3]; PC_4 = out_3[4];
  //   PC_5 = out_3[5]; PC_6 = out_3[6]; PC_7 = out_3[7]; PC_8 = out_3[8]; PC_9 = out_3[9]; PC_10 = out_3[10];
  //   PC_11 = out_3[11]; DR_0_t = out_4[0]; DR_1 = out_4[1]; DR_2 = out_4[2]; DR_3 = out_4[3]; DR_4 = out_4[4];
  //   DR_5 = out_4[5]; DR_6 = out_4[6]; DR_7 = out_4[7]; DR_8 = out_4[8]; DR_9 = out_4[9]; DR_10 = out_4[10];
  //   DR_11 = out_4[11]; DR_12 = out_4[12]; DR_13 = out_4[13]; DR_14 = out_4[14]; DR_15 = out_4[15];
  //   AC_0_t = out_5[0]; AC_1 = out_5[1]; AC_2 = out_5[2]; AC_3 = out_5[3]; AC_4 = out_5[4]; AC_5 = out_5[5];
  //   AC_6 = out_5[6]; AC_7 = out_5[7]; AC_8 = out_5[8]; AC_9 = out_5[9]; AC_10 = out_5[10]; AC_11 = out_5[11];
  //   AC_12 = out_5[12]; AC_13 = out_5[13]; AC_14 = out_5[14]; AC_15 = out_5[15]; TR_0 = out_9[0]; TR_1 = out_9[1];
  //   TR_2 = out_9[2]; TR_3 = out_9[3]; TR_4 = out_9[4]; TR_5 = out_9[5]; TR_6 = out_9[6]; TR_7 = out_9[7];
  //   TR_8 = out_9[8]; TR_9 = out_9[9]; TR_10 = out_9[10]; TR_11 = out_9[11]; TR_12 = out_9[12]; TR_13 = out_9[13];
  //   TR_14 = out_9[14]; TR_15 = out_9[15]; M_0 = out_10[0]; M_1 = out_10[1]; M_2 = out_10[2]; M_3 = out_10[3];
  //   M_4 = out_10[4]; M_5 = out_10[5]; M_6 = out_10[6]; M_7 = out_10[7]; M_8 = out_10[8]; M_9 = out_10[9];
  //   M_10 = out_10[10]; M_11 = out_10[11]; M_12 = out_10[12]; M_13 = out_10[13]; M_14 = out_10[14];
  //   M_15 = out_10[15]

  // Notes on the sheet:
  //   T
  //   R
  //   IEN
  //   FGI/FGO
  //   E
  //   S
  //   BUS
  //   SC
  //   D
  //   DR
  //   AC
  //   AR
  //   PC
  //   IR
  //   TR
  //   OUTR
  //   RAM
endmodule

// 16B_register
module register_16bit (
  input  LD,
  input  [15:0] in_2,
  input  INR,
  input  CLR,
  input  CLK,
  output [15:0] out_6
);

  Counter #(.width(16), .max('hffff)) counter_1 (
    .load(LD), .D(in_2), .count(INR), .Q(out_6), .clk(CLK), .clr(CLR));  // open: carry
endmodule

// 12bit_register
module register_12bit (
  input  LD,
  input  [11:0] in_2,
  input  INR,
  input  CLR,
  input  CLK,
  output [11:0] out_6
);

  Counter #(.width(12), .max('hfff)) counter_1 (
    .load(LD), .D(in_2), .count(INR), .Q(out_6), .clk(CLK), .clr(CLR));  // open: carry
endmodule

module INPR (
  input  [7:0] INPUT,
  input  FGI_NOT,
  output [7:0] OUTPUT
);

  Register register_1 (.D(INPUT), .en(FGI_NOT), .Q(OUTPUT));  // open: clk, clr
endmodule

module OUTR (
  input  LD,
  input  [7:0] in_2,
  input  CLK,
  output [7:0] out_4
);

  Counter counter_1 (.load(LD), .D(in_2), .count(1'b0), .Q(out_4), .clk(CLK));  // open: carry, clr
endmodule

module full_adder (
  input  x,
  input  y,
  input  cIn,
  output s,
  output cout
);

  wire and_1_out, and_2_out, xor_1_out;

  xor xor_1 (xor_1_out, x, y);
  xor xor_2 (s, xor_1_out, cIn);
  and and_1 (and_1_out, xor_1_out, cIn);
  and and_2 (and_2_out, x, y);
  or or_1 (cout, and_1_out, and_2_out);
endmodule

module ALU (
  input  [6:0] CNTRL,
  input  [15:0] DR,
  input  [15:0] AC,
  input  [7:0] INPR,
  input  E,
  output E_OUT,
  output [15:0] OUT
);

  wire and_1_out, and_2_out, and_3_out, and_4_out, carry_out, CNTRL1, one_bit_ALU_2_cout, one_bit_ALU_3_cout,
       one_bit_ALU_4_cout, one_bit_ALU_5_cout, one_bit_ALU_6_cout, one_bit_ALU_7_cout, one_bit_ALU_8_cout,
       one_bit_ALU_9_cout, one_bit_ALU_10_cout, one_bit_ALU_11_cout, one_bit_ALU_12_cout,
       one_bit_ALU_13_cout, one_bit_ALU_14_cout, one_bit_ALU_15_cout, one_bit_ALU_cout, or_1_out;

  or or_1 (or_1_out, CNTRL[0], CNTRL1, CNTRL[6]);
  and and_1 (and_1_out, CNTRL[0], carry_out);
  and and_2 (and_2_out, CNTRL[5], AC[0]);
  and and_3 (and_3_out, CNTRL[6], AC[15]);
  and and_4 (and_4_out, E, ~or_1_out);  // AND_Gate
  or or_2 (E_OUT, and_1_out, and_2_out, and_3_out, and_4_out);
  one_bit_ALU one_bit_ALU (
    .AC_i_1(AC[1]), .AC_i_1_2(E), .Cout(one_bit_ALU_cout), .OUT(OUT[0]), .INPR(INPR[0]), .ACi(AC[0]),
    .DRi(DR[0]), .Cin(1'b0), .CNTRL(CNTRL));
  one_bit_ALU one_bit_ALU_2 (
    .AC_i_1(AC[2]), .AC_i_1_2(AC[0]), .Cout(one_bit_ALU_2_cout), .OUT(OUT[1]), .INPR(INPR[1]), .ACi(AC[1]),
    .DRi(DR[1]), .Cin(one_bit_ALU_cout), .CNTRL(CNTRL));
  one_bit_ALU one_bit_ALU_3 (
    .AC_i_1(AC[3]), .AC_i_1_2(AC[1]), .Cout(one_bit_ALU_3_cout), .OUT(OUT[2]), .INPR(INPR[2]), .ACi(AC[2]),
    .DRi(DR[2]), .Cin(one_bit_ALU_2_cout), .CNTRL(CNTRL));
  one_bit_ALU one_bit_ALU_4 (
    .AC_i_1(AC[4]), .AC_i_1_2(AC[2]), .Cout(one_bit_ALU_4_cout), .OUT(OUT[3]), .INPR(INPR[3]), .ACi(AC[3]),
    .DRi(DR[3]), .Cin(one_bit_ALU_3_cout), .CNTRL(CNTRL));
  one_bit_ALU one_bit_ALU_5 (
    .AC_i_1(AC[5]), .AC_i_1_2(AC[3]), .Cout(one_bit_ALU_5_cout), .OUT(OUT[4]), .INPR(INPR[4]), .ACi(AC[4]),
    .DRi(DR[4]), .Cin(one_bit_ALU_4_cout), .CNTRL(CNTRL));
  one_bit_ALU one_bit_ALU_6 (
    .AC_i_1(AC[6]), .AC_i_1_2(AC[4]), .Cout(one_bit_ALU_6_cout), .OUT(OUT[5]), .INPR(INPR[5]), .ACi(AC[5]),
    .DRi(DR[5]), .Cin(one_bit_ALU_5_cout), .CNTRL(CNTRL));
  one_bit_ALU one_bit_ALU_7 (
    .AC_i_1(AC[7]), .AC_i_1_2(AC[5]), .Cout(one_bit_ALU_7_cout), .OUT(OUT[6]), .INPR(INPR[6]), .ACi(AC[6]),
    .DRi(DR[6]), .Cin(one_bit_ALU_6_cout), .CNTRL(CNTRL));
  one_bit_ALU one_bit_ALU_8 (
    .AC_i_1(AC[8]), .AC_i_1_2(AC[6]), .Cout(one_bit_ALU_8_cout), .OUT(OUT[7]), .INPR(INPR[7]), .ACi(AC[7]),
    .DRi(DR[7]), .Cin(one_bit_ALU_7_cout), .CNTRL(CNTRL));
  one_bit_ALU one_bit_ALU_9 (
    .AC_i_1(AC[9]), .AC_i_1_2(AC[7]), .Cout(one_bit_ALU_9_cout), .OUT(OUT[8]), .INPR(1'b0), .ACi(AC[8]),
    .DRi(DR[8]), .Cin(one_bit_ALU_8_cout), .CNTRL(CNTRL));
  one_bit_ALU one_bit_ALU_10 (
    .AC_i_1(AC[10]), .AC_i_1_2(AC[8]), .Cout(one_bit_ALU_10_cout), .OUT(OUT[9]), .INPR(1'b0), .ACi(AC[9]),
    .DRi(DR[9]), .Cin(one_bit_ALU_9_cout), .CNTRL(CNTRL));
  one_bit_ALU one_bit_ALU_11 (
    .AC_i_1(AC[11]), .AC_i_1_2(AC[9]), .Cout(one_bit_ALU_11_cout), .OUT(OUT[10]), .INPR(1'b0), .ACi(AC[10]),
    .DRi(DR[10]), .Cin(one_bit_ALU_10_cout), .CNTRL(CNTRL));
  one_bit_ALU one_bit_ALU_12 (
    .AC_i_1(AC[12]), .AC_i_1_2(AC[10]), .Cout(one_bit_ALU_12_cout), .OUT(OUT[11]), .INPR(1'b0), .ACi(AC[11]),
    .DRi(DR[11]), .Cin(one_bit_ALU_11_cout), .CNTRL(CNTRL));
  one_bit_ALU one_bit_ALU_13 (
    .AC_i_1(AC[13]), .AC_i_1_2(AC[11]), .Cout(one_bit_ALU_13_cout), .OUT(OUT[12]), .INPR(1'b0), .ACi(AC[12]),
    .DRi(DR[12]), .Cin(one_bit_ALU_12_cout), .CNTRL(CNTRL));
  one_bit_ALU one_bit_ALU_14 (
    .AC_i_1(AC[14]), .AC_i_1_2(AC[12]), .Cout(one_bit_ALU_14_cout), .OUT(OUT[13]), .INPR(1'b0), .ACi(AC[13]),
    .DRi(DR[13]), .Cin(one_bit_ALU_13_cout), .CNTRL(CNTRL));
  one_bit_ALU one_bit_ALU_15 (
    .AC_i_1(AC[15]), .AC_i_1_2(AC[13]), .Cout(one_bit_ALU_15_cout), .OUT(OUT[14]), .INPR(1'b0), .ACi(AC[14]),
    .DRi(DR[14]), .Cin(one_bit_ALU_14_cout), .CNTRL(CNTRL));
  one_bit_ALU one_bit_ALU_16 (
    .AC_i_1(E), .AC_i_1_2(AC[14]), .Cout(carry_out), .OUT(OUT[15]), .INPR(1'b0), .ACi(AC[15]), .DRi(DR[15]),
    .Cin(one_bit_ALU_15_cout), .CNTRL(CNTRL));
endmodule

module one_bit_ALU (
  input  INPR,
  input  ACi,
  input  DRi,
  input  Cin,
  input  AC_i_1,
  input  AC_i_1_2,
  input  [6:0] CNTRL,
  output Cout,
  output OUT
);

  wire and_1_out, and_2_out, and_3_out, and_4_out, and_5_out, and_6_out, and_7_out, FA_s, not_1_out;

  full_adder FA (.x(DRi), .y(ACi), .cIn(Cin), .s(FA_s), .cout(Cout));
  not not_1 (not_1_out, ACi);
  and and_1 (and_1_out, CNTRL[0], DRi, ACi);
  and and_2 (and_2_out, CNTRL[1], FA_s);
  and and_3 (and_3_out, CNTRL[2], DRi);
  and and_4 (and_4_out, CNTRL[3], INPR);
  and and_5 (and_5_out, CNTRL[4], not_1_out);
  and and_6 (and_6_out, CNTRL[5], AC_i_1);
  and and_7 (and_7_out, CNTRL[6], AC_i_1_2);
  or or_1 (OUT, and_1_out, and_2_out, and_3_out, and_4_out, and_5_out, and_6_out, and_7_out);

  // Other names for the same wires on the sheet: AND = CNTRL[0]; ADD = CNTRL[1]; DR = CNTRL[2]; INP = CNTRL[3];
  //   COM = CNTRL[4]; SHR = CNTRL[5]; SHL = CNTRL[6]
endmodule
